// Logisim project atto-8.circ as structural Verilog: 1 circuit, main circuit main
module main (
);

  wire and_1_out, and_4_out, and_5_out, button_1_out, CIN, CLK, CLR_SC, controlled_buffer_11_out,
       counter_2_carry, counter_3_carry, COUT, DATA_AL, DATA_CF, DATA_IL, DATA_IP, DATA_MEM, DATA_SP,
       DATA_XL, DATA_YL, DATA_ZL, DISPLAY, IP_DATA, keyboard_1_avail, MEM_DATA, NAND_DATA, not_1_out,
       not_2_out, not_3_out, not_4_out, not_5_out, not_6_out, not_7_out, not_8_out, not_10_out, or_1_out,
       or_2_out, or_3_out, PULL, RST, s_r_ff_1_q, s_r_ff_1_qn, SP_DATA, STDIN, STDOUT, SUM_DATA, ZERO;
  wire [4:0] counter_1_q, counter_2_q, undriven;
  wire [5:5] register_8_q;
  wire [6:0] keyboard_1_data;
  wire [7:0] adder_1_out, ADDR, button_2_out, DATA, demultiplexer_1_out0, demultiplexer_1_out1,
       demultiplexer_1_out2, demultiplexer_1_out3, demultiplexer_1_out4, demultiplexer_1_out5,
       demultiplexer_1_out6, demultiplexer_1_out7, demultiplexer_1_out8, demultiplexer_1_out9,
       demultiplexer_1_out10, demultiplexer_1_out11, demultiplexer_1_out12, demultiplexer_1_out13,
       demultiplexer_1_out14, demultiplexer_1_out15, demultiplexer_1_out16, demultiplexer_1_out17,
       demultiplexer_1_out18, demultiplexer_1_out19, demultiplexer_1_out20, demultiplexer_1_out21,
       demultiplexer_1_out22, demultiplexer_1_out23, demultiplexer_1_out24, demultiplexer_1_out25,
       demultiplexer_1_out26, demultiplexer_1_out27, demultiplexer_1_out28, demultiplexer_1_out29,
       demultiplexer_1_out30, demultiplexer_1_out31, ledbar_10_p1, MEMADDR, MEMDATA, multiplexer_1_out,
       nand_1_out, or_4_out, pull_resistor_1_node, register_1_q, register_2_q, register_3_q, register_4_q,
       register_5_q, ROM0_data;
  wire [7:7] not_9_out;
  wire [8:0] counter_3_q, undriven_2;

  not not_1 (not_1_out, STDIN);
  Register register_1 (.D(DATA), .en(DATA_XL), .clk(CLK), .Q(register_1_q), .clr(RST));
  // LedBar #(.inputtype("row")) ledbar_1: pin names not known; wires that end beside it: register_1_q
  Register register_2 (.D(DATA), .en(DATA_YL), .clk(CLK), .Q(register_2_q), .clr(RST));
  // LedBar #(.inputtype("row")) ledbar_2: pin names not known; wires that end beside it: register_2_q
  Register register_3 (.D(DATA), .en(DATA_ZL), .clk(CLK), .Q(register_3_q), .clr(RST));
  // LedBar #(.inputtype("row")) ledbar_3: pin names not known; wires that end beside it: register_3_q
  Register register_4 (.D(DATA), .en(DATA_IP), .clk(CLK), .Q(register_4_q), .clr(RST));
  // LedBar #(.inputtype("row")) ledbar_4: pin names not known; wires that end beside it: register_4_q
  Register register_5 (.D(DATA), .en(DATA_SP), .clk(CLK), .Q(register_5_q), .clr(RST));
  // LedBar #(.inputtype("row")) ledbar_5: pin names not known; wires that end beside it: register_5_q
  and and_1 (and_1_out, MEM_DATA, not_1_out);
  Counter #(.max('h1f), .width(5)) counter_1 (
    .clr(RST), .load(1'b0), .up(1'b1), .count(DISPLAY), .clk(not_2_out), .D(undriven), .Q(counter_1_q));  // open: carry
  not not_2 (not_2_out, CLK);
  // NoConnect on undriven
  RAM #(.asyncread("true"), .databus("bidir")) MEM (
    .addr(MEMADDR), .we(or_1_out), .oe(or_2_out), .clk(CLK), .data(MEMDATA));
  or or_1 (or_1_out, DATA_MEM, RST);
  or or_2 (or_2_out, and_1_out, DISPLAY);
  nor nor_1 (STDOUT, ADDR[0], ADDR[1], ADDR[2], ADDR[3], ADDR[4], ADDR[5], ADDR[6], ADDR[7]);
  S_R_Flip_Flop s_r_ff_1 (
    .S(STDOUT), .R(1'b0), .clk(not_3_out), .Q(s_r_ff_1_q), .reset(RST), .Qn(s_r_ff_1_qn), .preset(1'b0));
  not not_3 (not_3_out, MEM_DATA);
  Adder adder_1 (.a(register_1_q), .b(register_2_q), .out(adder_1_out), .cin(CIN), .cout(COUT));
  LED led_1 (.in(COUT));
  assign nand_1_out = ~(register_2_q & register_3_q);  // NAND_Gate nand_1, 8 bits wide
  nor nor_2 (ZERO, nand_1_out[0], nand_1_out[1], nand_1_out[2], nand_1_out[3], nand_1_out[4], nand_1_out[5], nand_1_out[6], nand_1_out[7]);
  assign DATA = IP_DATA ? register_4_q : 8'bz;  // Controlled_Buffer controlled_buffer_1
  assign DATA = SP_DATA ? register_5_q : 8'bz;  // Controlled_Buffer controlled_buffer_2
  assign MEMADDR = MEM_DATA ? ADDR : 8'bz;  // Controlled_Buffer controlled_buffer_3
  and and_2 (STDIN, STDOUT, s_r_ff_1_q);
  // NoConnect on s_r_ff_1_qn
  // LedBar #(.inputtype("row")) ledbar_6: pin names not known; wires that end beside it: adder_1_out
  LED led_2 (.in(CIN));
  // LedBar #(.inputtype("row")) ledbar_7: pin names not known; wires that end beside it: nand_1_out
  LED led_3 (.in(ZERO));
  // LedBar #(.inputtype("row")) ledbar_8: pin names not known; wires that end beside it: {8{1'b1}}
  assign MEMADDR = DATA_MEM ? ADDR : 8'bz;  // Controlled_Buffer controlled_buffer_4
  assign MEMADDR = DISPLAY ? {3'b111, counter_1_q} : 8'bz;  // Controlled_Buffer controlled_buffer_5
  assign DATA = SUM_DATA ? adder_1_out : 8'bz;  // Controlled_Buffer controlled_buffer_6
  assign DATA = NAND_DATA ? nand_1_out : 8'bz;  // Controlled_Buffer controlled_buffer_7
  assign DATA = PULL ? {8{1'b1}} : 8'bz;  // Controlled_Buffer controlled_buffer_8
  assign DATA = MEM_DATA ? MEMDATA : 8'bz;  // Controlled_Buffer controlled_buffer_9
  // LedBar #(.inputtype("row")) ledbar_9: pin names not known; wires that end beside it: DATA
  assign MEMDATA = DATA_MEM ? DATA : 8'bz;  // Controlled_Buffer controlled_buffer_10
  assign controlled_buffer_11_out = SUM_DATA ? COUT : 1'bz;  // Controlled_Buffer controlled_buffer_11
  assign controlled_buffer_11_out = NAND_DATA ? ZERO : 1'bz;  // Controlled_Buffer controlled_buffer_12
  // LedBar #(.inputtype("row")) ledbar_10: pin names not known; wires that end beside it: ledbar_10_p1
  // LedBar #(.inputtype("row")) ledbar_11: pin names not known; wires that end beside it: ADDR
  Pull_Resistor pull_resistor_1 (.node(pull_resistor_1_node));
  assign pull_resistor_1_node = DISPLAY ? MEMDATA : 8'bz;  // Controlled_Buffer controlled_buffer_13
  Demultiplexer #(.enable("true"), .select(5), .width(8)) demultiplexer_1 (
    .out0(demultiplexer_1_out0), .out1(demultiplexer_1_out1), .out2(demultiplexer_1_out2),
    .out3(demultiplexer_1_out3), .out4(demultiplexer_1_out4), .out5(demultiplexer_1_out5),
    .out6(demultiplexer_1_out6), .out7(demultiplexer_1_out7), .out8(demultiplexer_1_out8),
    .out9(demultiplexer_1_out9), .out10(demultiplexer_1_out10), .out11(demultiplexer_1_out11),
    .out12(demultiplexer_1_out12), .out13(demultiplexer_1_out13), .out14(demultiplexer_1_out14),
    .out15(demultiplexer_1_out15), .out16(demultiplexer_1_out16), .out17(demultiplexer_1_out17),
    .out18(demultiplexer_1_out18), .out19(demultiplexer_1_out19), .out20(demultiplexer_1_out20),
    .out21(demultiplexer_1_out21), .out22(demultiplexer_1_out22), .out23(demultiplexer_1_out23),
    .out24(demultiplexer_1_out24), .out25(demultiplexer_1_out25), .out26(demultiplexer_1_out26),
    .out27(demultiplexer_1_out27), .out28(demultiplexer_1_out28), .out29(demultiplexer_1_out29),
    .out30(demultiplexer_1_out30), .out31(demultiplexer_1_out31), .in(pull_resistor_1_node),
    .sel(counter_1_q), .en(CLK));
  Counter #(.max('h1f), .width(5)) counter_2 (
    .clr(or_3_out), .load(1'b0), .up(1'b1), .count(not_4_out), .clk(not_5_out), .D({5{1'b1}}),
    .carry(counter_2_carry), .Q(counter_2_q));
  or or_3 (or_3_out, RST, CLR_SC);
  not not_4 (not_4_out, RST);
  not not_5 (not_5_out, CLK);
  Register register_6 (.D(DATA), .en(DATA_IL), .clk(CLK), .Q(ledbar_10_p1), .clr(RST));
  Register register_7 (.D(DATA), .en(DATA_AL), .clk(CLK), .Q(ADDR), .clr(RST));
  not not_6 (not_6_out, MEM_DATA);
  not not_7 (not_7_out, DATA_MEM);
  not not_8 (not_8_out, RST);
  // LedBar #(.inputtype("row"), .matrixcols(5)) ledbar_12: pin names not known; wires that end beside it: counter_2_q
  Register #(.width(1)) register_8 (
    .D(controlled_buffer_11_out), .en(DATA_CF), .clk(CLK), .Q(register_8_q[5]), .clr(RST));
  not not_9 (not_9_out[7], ledbar_10_p1[7]);
  and and_3 (DISPLAY, not_6_out, not_7_out, not_8_out);
  DotMatrix #(.inputtype("row"), .matrixcols(8), .matrixrows(8), .persist(96)) dotmatrix_1 (
    .row0(demultiplexer_1_out0), .row1(demultiplexer_1_out2), .row2(demultiplexer_1_out4),
    .row3(demultiplexer_1_out6), .row4(demultiplexer_1_out8), .row5(demultiplexer_1_out10),
    .row6(demultiplexer_1_out12), .row7(demultiplexer_1_out14));
  DotMatrix #(.inputtype("row"), .matrixcols(8), .matrixrows(8), .persist(96)) dotmatrix_2 (
    .row0(demultiplexer_1_out16), .row1(demultiplexer_1_out18), .row2(demultiplexer_1_out20),
    .row3(demultiplexer_1_out22), .row4(demultiplexer_1_out24), .row5(demultiplexer_1_out26),
    .row6(demultiplexer_1_out28), .row7(demultiplexer_1_out30));
  // NoConnect on counter_2_carry
  LedBar #(.matrixcols(1)) ledbar_13 (.led0(register_8_q[5]));
  Clock clock_1 (.out(CLK));
  Button button_1 (.out(button_1_out));
  not not_10 (not_10_out, CLK);
  // DotMatrix #(.inputtype("row"), .matrixcols(8), .matrixrows(8), .persist(96)) dotmatrix_3: pin names not known; wires that end beside it: demultiplexer_1_out1, demultiplexer_1_out3, demultiplexer_1_out5, demultiplexer_1_out7, demultiplexer_1_out9
  // DotMatrix #(.inputtype("row"), .matrixcols(8), .matrixrows(8), .persist(96)) dotmatrix_4: pin names not known; wires that end beside it: demultiplexer_1_out11, demultiplexer_1_out13, demultiplexer_1_out15, demultiplexer_1_out17, demultiplexer_1_out19, demultiplexer_1_out21, demultiplexer_1_out23, demultiplexer_1_out25, demultiplexer_1_out27, demultiplexer_1_out29, demultiplexer_1_out31
  // NoConnect on or_4_out[7]
  assign or_4_out = {{4{not_9_out[7]}}, 4'b0000} | ledbar_10_p1;  // OR_Gate or_4, 8 bits wide
  Counter #(.max('h1ff), .width(9)) counter_3 (
    .clr(button_1_out), .load(1'b0), .up(1'b1), .count(RST), .clk(not_10_out), .D(undriven_2),
    .carry(counter_3_carry), .Q(counter_3_q));
  // NoConnect on undriven_2
  ROM #(.addrWidth(13), .dataWidth(16)) MIC (
    .addr({or_4_out[6:0], register_8_q[5], counter_2_q}),
    .data({DATA_IP, DATA_SP, DATA_CF, DATA_IL, DATA_AL, DATA_XL, DATA_YL, DATA_ZL, IP_DATA, SP_DATA, MEM_DATA, DATA_MEM, CLR_SC, CIN, SUM_DATA, NAND_DATA}));
  // NoConnect on counter_3_carry
  assign MEMADDR = RST ? counter_3_q[7:0] : 8'bz;  // Controlled_Buffer controlled_buffer_14
  ROM ROM0 (.addr(counter_3_q[7:0]), .data(ROM0_data));
  not not_11 (RST, counter_3_q[8]);
  // NoConnect on DATA[7]
  TTY tty_1 (.data(DATA[6:0]), .clk(CLK), .we(and_4_out), .clr(RST));
  and and_4 (and_4_out, STDOUT, DATA_MEM);
  Keyboard #(.buflen(256)) keyboard_1 (
    .clk(CLK), .re(and_5_out), .clr(RST), .avail(keyboard_1_avail), .data(keyboard_1_data));
  and and_5 (and_5_out, MEM_DATA, STDIN);
  Button button_2 (.out(button_2_out[0]));
  Button button_3 (.out(button_2_out[2]));
  Button button_4 (.out(button_2_out[3]));
  Button button_5 (.out(button_2_out[1]));
  // LedBar #(.inputtype("row"), .matrixcols(16)) ledbar_14: pin names not known; wires that end beside it: {DATA_IP, DATA_SP, DATA_CF, DATA_IL, DATA_AL, DATA_XL, DATA_YL, DATA_ZL, IP_DATA, SP_DATA, MEM_DATA, DATA_MEM, CLR_SC, CIN, SUM_DATA, NAND_DATA}
  LED led_4 (.in(PULL));
  nor nor_3 (PULL, IP_DATA, SP_DATA, MEM_DATA, SUM_DATA, NAND_DATA);
  Button button_6 (.out(button_2_out[4]));
  Button button_7 (.out(button_2_out[6]));
  Button button_8 (.out(button_2_out[7]));
  Button button_9 (.out(button_2_out[5]));
  assign MEMDATA = RST ? ROM0_data : 8'bz;  // Controlled_Buffer controlled_buffer_15
  Multiplexer #(.width(8)) multiplexer_1 (
    .in0(button_2_out), .in1({1'b0, keyboard_1_data}), .out(multiplexer_1_out), .sel(keyboard_1_avail));
  assign MEMDATA = and_5_out ? multiplexer_1_out : 8'bz;  // Controlled_Buffer controlled_buffer_16

  // Other names for the same wires on the sheet: SET_CIN = CIN; WRT = DATA_MEM; READ = MEM_DATA

  // Notes on the sheet:
  //   XL
  //   YL
  //   ZL
  //   IP
  //   SP
  //   SUM
  //   NAND
  //   ONES
  //   ADDR
  //   MEM
  //   COUT
  //   CIN
  //   ZERO
  //   DATA
  //   IL
  //   AL
  //   SC
  //   CF
  //   . . . . . . . . . . . . . . . . . . . . . . . . . . . . . . . . . . . . . . . . . . . . . . . . . . . . . . . . . . . . . . . . . . . . . . . . . . . . . . . . . . . . . . . . . . . . . . . . . . . . . . . . . . . . . . . . . . . . . . . . . . . . . . . . . . . . . . . . . . . . . . . . . . . . . . . . . . . . . . . . . . . . . . . . 
  //   CLK
  //   RST
  //   DISPLAY
  //   MIC
  //   PULL
  //   Atto-8 Microprocessor
  //   Atto-8 Microcomputer
  //   STDIO
  //   CTRL
endmodule
